# Fritzing sketch Sensors_and_Monitoring_Systems_final_project (saved by Fritzing 1.0.7)
breadboards: 1

parts:
  Part1 = Arduino Uno (Rev3)
  S1 = Pushbutton [package="[THT]"]
  Adafruit_Simple_Soil_Moisture_Sensor1 = Adafruit Simple Soil Moisture Sensor [mn=Adafruit mpn=#6362 part_number=#6362]
  Part2 = Adafruit HUZZAH ESP8266 [part_number="Adafruit #2471"]

nets:
  N1: Part1.A0, Adafruit_Simple_Soil_Moisture_Sensor1.SIGNAL
  N2: Part1.D10_PWM/SS, Part2.TX
  N3: Part1.D11_PWM/MOSI, Part2.RX
  GND: Part1.GND, S1.Pin_3, S1.Pin_4, Adafruit_Simple_Soil_Moisture_Sensor1.GND, Part2.GND
  N4: Part1.D2, S1.Pin_1, S1.Pin_2
  3V3: Part1.3V3, Part2.VIN
  N5: Part1.5V, Adafruit_Simple_Soil_Moisture_Sensor1.V+
